# Fritzing sketch air_exchange_timer (saved by Fritzing 0.9.3b)
breadboards: 1

parts:
  The_Nano1 = Arduino Nano (Rev3.0)
  LED_2_9 = ws2812b [package="smd 2812b"]
  S1 = Round Pushbutton
  LED_2_10 = ws2812b [package="smd 2812b"]
  LED_2_11 = ws2812b [package="smd 2812b"]

nets:
  VSS: The_Nano1.GND, LED_2_9.VSS, S1.leg0, LED_2_10.VSS, LED_2_11.VSS
  N1: The_Nano1.D2, LED_2_9.DIN
  N2: The_Nano1.D3, S1.leg1
  VDD: The_Nano1.5V, LED_2_9.VDD, LED_2_10.VDD, LED_2_11.VDD
  N3: LED_2_9.DOUT, LED_2_10.DIN
  N4: LED_2_10.DOUT, LED_2_11.DIN
